// Logisim project Lab2.circ as structural Verilog: 1 circuit, main circuit main
module main (
  input  A,
  input  B,
  input  Cin,
  output Cout,
  output Cout_2,
  output Sum,
  output Sum_2
);

  wire not_1_out;

  not not_1 (not_1_out, B);
  Adder #(.width(1)) adder_1 (.a(A), .b(B), .out(Cout), .cin(Cin), .cout(Cout));
  Multiplexer #(.select(2), .enable("false")) multiplexer_1 (
    .in0(A), .in1(B), .in2(B), .in3(A), .out(Cout_2), .sel({Cin, A}));
  Multiplexer #(.select(2), .enable("false")) multiplexer_2 (
    .in1(not_1_out), .out(Sum_2), .sel({Cin, A}));  // open: in0, in2, in3

  assign Sum = Cout;
endmodule
